// Logisim project Fig 1.circ as structural Verilog: 1 circuit, main circuit main
module main (
  input  IN,
  output UNLOCK
);

  wire and_1_out, and_2_out, and_3_out, and_4_out, clock_1_out, not_1_out, or_1_out, or_2_out, Q0_q, Q1_q,
       Q1_qn, Q2_q, Q2_qn, xor_1_out;

  Clock clock_1 (.out(clock_1_out));
  not not_1 (not_1_out, IN);
  D_Flip_Flop Q2 (.clk(clock_1_out), .D(IN), .Q(Q2_q), .Qn(Q2_qn), .preset(1'b0), .reset(1'b0));  // open: en
  D_Flip_Flop Q1 (.clk(clock_1_out), .D(or_1_out), .Q(Q1_q), .Qn(Q1_qn), .preset(1'b0), .reset(1'b0));  // open: en
  D_Flip_Flop Q0 (.clk(clock_1_out), .D(or_2_out), .Q(Q0_q), .preset(1'b0), .reset(1'b0));  // open: Qn, en
  and and_1 (and_1_out, Q0_q, Q1_qn, Q2_qn, IN);
  and and_2 (and_2_out, Q2_q, not_1_out);
  and and_3 (and_3_out, Q1_q, Q2_qn);
  xor xor_1 (xor_1_out, Q2_q, Q0_q);
  or or_1 (or_1_out, and_1_out, and_2_out);
  and and_4 (and_4_out, and_2_out, Q0_q);
  and and_5 (UNLOCK, xor_1_out, Q1_q);
  or or_2 (or_2_out, and_4_out, and_3_out);
endmodule
