// Logisim project LAB 10.circ as structural Verilog: 3 circuits, main circuit ROM
module ROM (
  input  [5:0] in_1,
  output HG,
  output HY,
  output HR,
  output FG,
  output FY,
  output FR
);

  wire clock_1_out;
  wire [5:0] Q_star_q, rom_1_data;

  ROM_part #(.addrWidth(6), .dataWidth(6)) rom_1 (.addr(in_1), .data(rom_1_data));  // open: sel
  Clock clock_1 (.out(clock_1_out));
  Register #(.width(6)) Q (.D(Q_star_q), .clk(clock_1_out));  // open: en, Q, clr
  Register #(.width(6)) Q_star (.D(rom_1_data), .Q(Q_star_q), .clk(clock_1_out));  // open: en, clr
  Register #(.width(3)) register_1 (.D(rom_1_data[2:0]), .en(1'b1), .Q({HR, HY, HG}), .clk(clock_1_out));  // open: clr
  Register #(.width(3)) register_2 (.D(rom_1_data[5:3]), .en(1'b1), .Q({FR, FY, FG}), .clk(clock_1_out));  // open: clr

  // Notes on the sheet:
  //   contents of rom_1 (hex, n*v repeats v):
  //   16*c a a a 9 16*21 11 11 11 9
endmodule

module Counter (
  input  C,
  input  RESET,
  output [5:0] out_3
);

  wire and_1_out, clock_1_out, comparator_1_eq, not_1_out, or_1_out;
  wire [5:0] counter_1_q;

  not not_1 (not_1_out, C);
  and and_1 (and_1_out, comparator_1_eq, not_1_out);
  or or_1 (or_1_out, and_1_out, RESET);
  Clock clock_1 (.out(clock_1_out));
  Counter_part #(.width(6), .max('h27)) counter_1 (
    .load(or_1_out), .D(6'b001111), .Q(counter_1_q), .clk(clock_1_out));  // open: count, carry, clr
  Comparator #(.width(6)) comparator_1 (.a(6'b001111), .b(counter_1_q), .eq(comparator_1_eq));  // open: gt, lt
  Multiplexer #(.width(6)) multiplexer_1 (.in0(counter_1_q), .in1(6'b010011), .out(out_3), .sel(RESET));  // open: en
endmodule

module main (
  input  C,
  input  RESET
);

  wire Datapath_fg, Datapath_fr, Datapath_fy, Datapath_hg, Datapath_hr, Datapath_hy;
  wire [5:0] Controller_out_3;

  Counter Controller (.C(C), .RESET(RESET), .out_3(Controller_out_3));
  LED HLR (.in(Datapath_hg));
  LED HLY (.in(Datapath_hy));
  ROM Datapath (
    .in_1(Controller_out_3), .HG(Datapath_hg), .HY(Datapath_hy), .HR(Datapath_hr), .FG(Datapath_fg),
    .FY(Datapath_fy), .FR(Datapath_fr));
  LED HLG (.in(Datapath_hr));
  LED FLR (.in(Datapath_fg));
  LED FLY (.in(Datapath_fy));
  LED FLG (.in(Datapath_fr));
endmodule
