// Logisim project Lab 11.circ as structural Verilog: 4 circuits, main circuit Datapath
// Data Unit
module Datapath (
  input  [2:0] D_Address,
  input  RegFileWrite,
  input  CLK,
  input  [2:0] A_Address,
  input  [2:0] B_Address,
  input  [3:0] ConstIN,
  input  Mux_B,
  input  [3:0] Function_Select,
  input  [3:0] DataIN,
  input  MuxF,
  output [3:0] AddrOut,
  output [3:0] DataOut,
  output [2:0] PZN
);

  wire [3:0] function_select_1_f, multiplexer_2_out, n8x4_regfile_1_bout;

  _8x4_RegFile u_8x4_regfile_1 (
    .D_In(multiplexer_2_out), .D_Address(D_Address), .RegFileWrite(RegFileWrite), .CLK(CLK),
    .A_Address(A_Address), .B_Address(B_Address), .AOut(AddrOut), .BOut(n8x4_regfile_1_bout));
  Multiplexer #(.width(4)) multiplexer_1 (
    .in0(n8x4_regfile_1_bout), .in1(ConstIN), .out(DataOut), .sel(Mux_B));  // open: en
  Function_Select function_select_1 (
    .A(AddrOut), .B(DataOut), .Function_Select(Function_Select), .F(function_select_1_f), .PZN(PZN));
  Multiplexer #(.width(4)) multiplexer_2 (
    .in0(function_select_1_f), .in1(DataIN), .out(multiplexer_2_out), .sel(MuxF));  // open: en
endmodule

module Function_Select (
  input  [3:0] A,
  input  [3:0] B,
  input  [3:0] Function_Select,
  output [3:0] F,
  output [2:0] PZN
);

  wire [3:0] adder_1_out, adder_2_out, and_1_out, divider_1_out, multiplier_1_out, not_1_out, not_2_out,
       or_1_out, shifter_1_out, shifter_2_out, shifter_3_out, subtractor_1_out;

  Adder #(.width(4)) adder_1 (.a(A), .b(B), .out(adder_1_out));  // open: cin, cout
  Subtractor #(.width(4)) subtractor_1 (.a(A), .b(B), .out(subtractor_1_out));  // open: bin, bout
  Multiplier #(.width(4)) multiplier_1 (.a(A), .b(B), .out(multiplier_1_out));  // open: cin, cout
  Divider #(.width(4)) divider_1 (.a(A), .b(A), .out(divider_1_out));  // open: upper, rem
  assign not_1_out = ~A;  // NOT_Gate not_1, 4 bits wide
  assign and_1_out = A & B;  // AND_Gate and_1, 4 bits wide
  assign or_1_out = A | B;  // OR_Gate or_1, 4 bits wide
  assign not_2_out = ~A;  // NOT_Gate not_2, 4 bits wide
  Shifter #(.width(4), .shift("lr")) shifter_1 (.in(A), .\dist (2'b01), .out(shifter_1_out));
  Shifter #(.width(4)) shifter_2 (.in(A), .\dist (2'b01), .out(shifter_2_out));
  Shifter #(.width(4), .shift("ar")) shifter_3 (.in(A), .\dist (2'b01), .out(shifter_3_out));
  Adder #(.width(4)) adder_2 (.a(not_2_out), .b(4'b0001), .out(adder_2_out));  // open: cin, cout
  Multiplexer #(.select(4), .width(4)) multiplexer_1 (
    .in0(4'b0000), .in1(4'b0001), .in2(A), .in3(B), .in4(adder_1_out), .in5(subtractor_1_out),
    .in6(multiplier_1_out), .in7(divider_1_out), .in8(not_1_out), .in9(and_1_out), .in10(or_1_out),
    .in11(adder_2_out), .in12(shifter_1_out), .in13(shifter_2_out), .in14(shifter_3_out), .out(F),
    .sel(Function_Select));  // open: in15, en
  Comparator #(.width(4)) comparator_1 (.a(F), .b(4'b0000), .gt(PZN[0]), .eq(PZN[1]), .lt(PZN[2]));
endmodule

module _8x4_RegFile (
  input  RegFileWrite,
  input  [3:0] D_In,
  input  [2:0] A_Address,
  input  [2:0] B_Address,
  input  [2:0] D_Address,
  input  CLK,
  output [3:0] AOut,
  output [3:0] BOut
);

  wire and_1_out, and_2_out, and_3_out, and_4_out, and_5_out, and_6_out, and_7_out, and_8_out,
       demultiplexer_1_out0, demultiplexer_1_out1, demultiplexer_1_out2, demultiplexer_1_out3,
       demultiplexer_1_out4, demultiplexer_1_out5, demultiplexer_1_out6, demultiplexer_1_out7;
  wire [3:0] R0_q, R1_q, R2_q, R3_q, R4_q, R5_q, R6_q, R7_q;

  Demultiplexer #(.select(3)) demultiplexer_1 (
    .out0(demultiplexer_1_out0), .out1(demultiplexer_1_out1), .out2(demultiplexer_1_out2),
    .out3(demultiplexer_1_out3), .out4(demultiplexer_1_out4), .out5(demultiplexer_1_out5),
    .out6(demultiplexer_1_out6), .out7(demultiplexer_1_out7), .in(1'b1), .sel(D_Address));  // open: en
  and and_1 (and_1_out, demultiplexer_1_out0, RegFileWrite);
  and and_2 (and_2_out, demultiplexer_1_out1, RegFileWrite);
  and and_3 (and_3_out, demultiplexer_1_out2, RegFileWrite);
  and and_4 (and_4_out, demultiplexer_1_out3, RegFileWrite);
  and and_5 (and_5_out, demultiplexer_1_out4, RegFileWrite);
  and and_6 (and_6_out, demultiplexer_1_out5, RegFileWrite);
  and and_7 (and_7_out, demultiplexer_1_out6, RegFileWrite);
  and and_8 (and_8_out, demultiplexer_1_out7, RegFileWrite);
  Register #(.width(4)) R0 (.D(D_In), .en(and_1_out), .Q(R0_q), .clk(CLK));  // open: clr
  Register #(.width(4)) R1 (.D(D_In), .en(and_2_out), .Q(R1_q), .clk(CLK));  // open: clr
  Register #(.width(4)) R2 (.en(and_3_out), .Q(R2_q), .clk(CLK));  // open: D, clr
  Register #(.width(4)) R3 (.D(D_In), .en(and_4_out), .Q(R3_q), .clk(CLK));  // open: clr
  Register #(.width(4)) R4 (.D(D_In), .en(and_5_out), .Q(R4_q), .clk(CLK));  // open: clr
  Register #(.width(4)) R5 (.D(D_In), .en(and_6_out), .Q(R5_q), .clk(CLK));  // open: clr
  Register #(.width(4)) R6 (.D(D_In), .en(and_7_out), .Q(R6_q), .clk(CLK));  // open: clr
  Register #(.width(4)) R7 (.D(D_In), .en(and_8_out), .Q(R7_q), .clk(CLK));  // open: clr
  Multiplexer #(.select(3), .width(4)) multiplexer_1 (
    .in0(R0_q), .in1(R1_q), .in2(R2_q), .in3(R3_q), .in4(R4_q), .in5(R5_q), .in6(R6_q), .in7(R7_q),
    .out(AOut), .sel(A_Address));  // open: en
  Multiplexer #(.select(3), .width(4)) multiplexer_2 (
    .in0(R0_q), .in1(R1_q), .in2(R2_q), .in3(R3_q), .in4(R4_q), .in5(R5_q), .in6(R6_q), .in7(R7_q),
    .out(BOut), .sel(B_Address));  // open: en
endmodule

module Data_Unit (
  input  [15:0] Control_Word,
  input  [3:0] Data_In,
  input  [3:0] Constant,
  output [3:0] Address_Out,
  output [3:0] Data_Out,
  output [2:0] PNZ
);

  wire clock_1_out;

  Clock clock_1 (.out(clock_1_out));
  Datapath datapath_1 (
    .D_Address(Control_Word[3:1]), .RegFileWrite(Control_Word[0]), .CLK(clock_1_out),
    .A_Address(Control_Word[15:13]), .B_Address(Control_Word[11:9]), .ConstIN(Constant),
    .Mux_B(Control_Word[12]), .Function_Select(Control_Word[7:4]), .MuxF(Control_Word[8]),
    .AddrOut(Address_Out), .DataOut(Data_Out), .PZN(PNZ), .DataIN(Data_In));
endmodule
