// Logisim project Lab 12.circ as structural Verilog: 11 circuits, main circuit Datapath
module Datapath (
  input  [15:0] Control_Word,
  input  CLK,
  input  [3:0] ConstIN,
  input  [3:0] DataIN,
  output [3:0] AddrOut,
  output [3:0] DataOut,
  output [2:0] PZN
);

  wire [3:0] function_select_1_f, multiplexer_2_out, n8x4_regfile_1_bout;

  _8x4_RegFile u_8x4_regfile_1 (
    .D_In(multiplexer_2_out), .D_Address(Control_Word[3:1]), .RegFileWrite(Control_Word[0]), .CLK(CLK),
    .A_Address(Control_Word[15:13]), .B_Address(Control_Word[11:9]), .AOut(AddrOut),
    .BOut(n8x4_regfile_1_bout));
  Multiplexer #(.width(4)) multiplexer_1 (
    .in0(n8x4_regfile_1_bout), .in1(ConstIN), .out(DataOut), .sel(Control_Word[12]));  // open: en
  Function_Select function_select_1 (
    .A(AddrOut), .B(DataOut), .Function_Select(Control_Word[7:4]), .F(function_select_1_f), .PZN(PZN));
  Multiplexer #(.width(4)) multiplexer_2 (
    .in0(function_select_1_f), .in1(DataIN), .out(multiplexer_2_out), .sel(Control_Word[8]));  // open: en
endmodule

module Function_Select (
  input  [3:0] A,
  input  [3:0] B,
  input  [3:0] Function_Select,
  output [3:0] F,
  output [2:0] PZN
);

  wire [3:0] adder_1_out, adder_2_out, and_1_out, divider_1_out, multiplier_1_out, not_1_out, not_2_out,
       or_1_out, shifter_1_out, shifter_2_out, shifter_3_out, subtractor_1_out;

  Adder #(.width(4)) adder_1 (.a(A), .b(B), .out(adder_1_out));  // open: cin, cout
  Subtractor #(.width(4)) subtractor_1 (.a(A), .b(B), .out(subtractor_1_out));  // open: bin, bout
  Multiplier #(.width(4)) multiplier_1 (.a(A), .b(B), .out(multiplier_1_out));  // open: cin, cout
  Divider #(.width(4)) divider_1 (.a(A), .b(A), .out(divider_1_out));  // open: upper, rem
  assign not_1_out = ~A;  // NOT_Gate not_1, 4 bits wide
  assign and_1_out = A & B;  // AND_Gate and_1, 4 bits wide
  assign or_1_out = A | B;  // OR_Gate or_1, 4 bits wide
  assign not_2_out = ~A;  // NOT_Gate not_2, 4 bits wide
  Shifter #(.width(4), .shift("lr")) shifter_1 (.in(A), .\dist (2'b01), .out(shifter_1_out));
  Shifter #(.width(4)) shifter_2 (.in(A), .\dist (2'b01), .out(shifter_2_out));
  Shifter #(.width(4), .shift("ar")) shifter_3 (.in(A), .\dist (2'b01), .out(shifter_3_out));
  Adder #(.width(4)) adder_2 (.a(not_2_out), .b(4'b0001), .out(adder_2_out));  // open: cin, cout
  Multiplexer #(.select(4), .width(4)) multiplexer_1 (
    .in0(4'b0000), .in1(4'b0001), .in2(A), .in3(B), .in4(adder_1_out), .in5(subtractor_1_out),
    .in6(multiplier_1_out), .in7(divider_1_out), .in8(not_1_out), .in9(and_1_out), .in10(or_1_out),
    .in11(adder_2_out), .in12(shifter_1_out), .in13(shifter_2_out), .in14(shifter_3_out), .out(F),
    .sel(Function_Select));  // open: in15, en
  Comparator #(.width(4)) comparator_1 (.a(F), .b(4'b0000), .gt(PZN[0]), .eq(PZN[1]), .lt(PZN[2]));
endmodule

module _8x4_RegFile (
  input  RegFileWrite,
  input  [3:0] D_In,
  input  [2:0] A_Address,
  input  [2:0] B_Address,
  input  [2:0] D_Address,
  input  CLK,
  output [3:0] AOut,
  output [3:0] BOut
);

  wire and_1_out, and_2_out, and_3_out, and_4_out, and_5_out, and_6_out, and_7_out, and_8_out,
       demultiplexer_1_out0, demultiplexer_1_out1, demultiplexer_1_out2, demultiplexer_1_out3,
       demultiplexer_1_out4, demultiplexer_1_out5, demultiplexer_1_out6, demultiplexer_1_out7;
  wire [3:0] R0_q, R1_q, R2_q, R3_q, R4_q, R5_q, R6_q, R7_q;

  Demultiplexer #(.select(3)) demultiplexer_1 (
    .out0(demultiplexer_1_out0), .out1(demultiplexer_1_out1), .out2(demultiplexer_1_out2),
    .out3(demultiplexer_1_out3), .out4(demultiplexer_1_out4), .out5(demultiplexer_1_out5),
    .out6(demultiplexer_1_out6), .out7(demultiplexer_1_out7), .in(1'b1), .sel(D_Address));  // open: en
  and and_1 (and_1_out, demultiplexer_1_out0, RegFileWrite);
  and and_2 (and_2_out, demultiplexer_1_out1, RegFileWrite);
  and and_3 (and_3_out, demultiplexer_1_out2, RegFileWrite);
  and and_4 (and_4_out, demultiplexer_1_out3, RegFileWrite);
  and and_5 (and_5_out, demultiplexer_1_out4, RegFileWrite);
  and and_6 (and_6_out, demultiplexer_1_out5, RegFileWrite);
  and and_7 (and_7_out, demultiplexer_1_out6, RegFileWrite);
  and and_8 (and_8_out, demultiplexer_1_out7, RegFileWrite);
  Register #(.width(4)) R0 (.D(D_In), .en(and_1_out), .Q(R0_q), .clk(CLK));  // open: clr
  Register #(.width(4)) R1 (.D(D_In), .en(and_2_out), .Q(R1_q), .clk(CLK));  // open: clr
  Register #(.width(4)) R2 (.D(D_In), .en(and_3_out), .Q(R2_q), .clk(CLK));  // open: clr
  Register #(.width(4)) R3 (.D(D_In), .en(and_4_out), .Q(R3_q), .clk(CLK));  // open: clr
  Register #(.width(4)) R4 (.D(D_In), .en(and_5_out), .Q(R4_q), .clk(CLK));  // open: clr
  Register #(.width(4)) R5 (.D(D_In), .en(and_6_out), .Q(R5_q), .clk(CLK));  // open: clr
  Register #(.width(4)) R6 (.D(D_In), .en(and_7_out), .Q(R6_q), .clk(CLK));  // open: clr
  Register #(.width(4)) R7 (.D(D_In), .en(and_8_out), .Q(R7_q), .clk(CLK));  // open: clr
  Multiplexer #(.select(3), .width(4)) multiplexer_1 (
    .in0(R0_q), .in1(R1_q), .in2(R2_q), .in3(R3_q), .in4(R4_q), .in5(R5_q), .in6(R6_q), .in7(R7_q),
    .out(AOut), .sel(A_Address));  // open: en
  Multiplexer #(.select(3), .width(4)) multiplexer_2 (
    .in0(R0_q), .in1(R1_q), .in2(R2_q), .in3(R3_q), .in4(R4_q), .in5(R5_q), .in6(R6_q), .in7(R7_q),
    .out(BOut), .sel(B_Address));  // open: en
endmodule

module Control_Unit (
  input  [15:0] Instruction,
  input  Start,
  input  [2:0] PZN,
  input  Reset,
  input  Clock,
  output [3:0] Constant,
  output [15:0] Control_Word,
  output Memory_Write,
  output Ready
);

  wire load_signal_logic_1_load, not_1_out;
  wire [7:0] control_address_register_1_address, data_signal_logic_1_data_out;
  wire [15:0] rom_1_data;
  wire [17:17] rom_1_data_2;

  Data_Signal_Logic data_signal_logic_1 (
    .Start(Start), .Mode(rom_1_data_2[17]), .Opcode_Instruction(Instruction[15:12]),
    .Next_Address(rom_1_data[11:4]), .Data_Out(data_signal_logic_1_data_out));
  Control_Address_Register control_address_register_1 (
    .Address(control_address_register_1_address), .Data_In(data_signal_logic_1_data_out), .Reset(Reset),
    .Load(load_signal_logic_1_load), .Clock(Clock));
  Generate_Ready generate_ready_1 (.Address(control_address_register_1_address), .Ready(Ready));
  Load_Signal_Logic load_signal_logic_1 (
    .PZN(PZN), .Start(Start), .Condition(rom_1_data[14:12]), .Mode(rom_1_data_2[17]), .Clock(Clock),
    .Load(load_signal_logic_1_load));
  Operand_Select operand_select_1 (
    .A_Operand(Instruction[11:8]), .B_Operand(Instruction[7:4]), .C_Operand(Instruction[3:0]),
    .Operand_Selector(rom_1_data[2:1]), .Constant(Constant));
  ROM #(.dataWidth(18)) rom_1 (
    .addr(control_address_register_1_address), .data({rom_1_data_2[17], Memory_Write, rom_1_data}));  // open: sel
  not not_1 (not_1_out, rom_1_data_2[17]);
  assign Control_Word = not_1_out ? rom_1_data : 16'bz;  // Controlled_Buffer controlled_buffer_1

  // Notes on the sheet:
  //   contents of rom_1 (hex, n*v repeats v):
  //   16*0 1033 1035 12400 13*0 1033 1035 4105 12400 12*0 1033 1035 1037 4105 6107 4645 12400 9*0 1033
  //   1035 1037 4105 6107 4655 12400 9*0 1033 1035 1037 4105 6107 4655 12400 9*0 1033 1035 4105 40c5 12400
  //   11*0 1033 1035 4105 4085 12400 11*0 1033 1035 1037 4105 6107 4695 12400 9*0 1033 1035 1037 4105 6107
  //   6029 22980 25990 12400 7*0 1033 1035 1037 4105 6107 4655 22a90 25a80 15 12400
endmodule

module Data_Signal_Logic (
  input  [3:0] Opcode_Instruction,
  input  [7:0] Next_Address,
  input  Start,
  input  Mode,
  output [7:0] Data_Out
);

  wire and_1_out, not_1_out;

  not not_1 (not_1_out, Start);
  and and_1 (and_1_out, not_1_out, Mode);
  Multiplexer #(.width(8)) multiplexer_1 (
    .in0({Opcode_Instruction, 4'b0000}), .in1(Next_Address), .out(Data_Out), .sel(and_1_out));  // open: en
endmodule

module Load_Signal_Logic (
  input  Start,
  input  [2:0] Condition,
  input  [2:0] PZN,
  input  Mode,
  input  Clock,
  output Load
);

  wire and_2_out, and_3_out, comparator_1_gt, d_ff_1_qn;
  wire [2:0] and_1_out, register_1_q;

  Register #(.width(3)) register_1 (.D(PZN), .Q(register_1_q), .clk(Clock));  // open: en, clr
  D_Flip_Flop d_ff_1 (.clk(Clock), .D(Start), .Qn(d_ff_1_qn));  // open: Q, preset, en, reset
  assign and_1_out = register_1_q & Condition;  // AND_Gate and_1, 3 bits wide
  Comparator #(.width(3), .mode("unsigned")) comparator_1 (
    .a(and_1_out), .b(3'b000), .gt(comparator_1_gt));  // open: eq, lt
  and and_2 (and_2_out, d_ff_1_qn, Start);
  and and_3 (and_3_out, comparator_1_gt, Mode);
  or or_1 (Load, and_2_out, and_3_out);
endmodule

module Control_Address_Register (
  input  [7:0] Data_In,
  input  Load,
  input  Reset,
  input  Clock,
  output [7:0] Address
);

  wire comparator_1_gt, or_1_out;
  wire [7:0] adder_1_out, multiplexer_1_out, multiplexer_2_out;

  Adder adder_1 (.a(Address), .b(8'h1), .out(adder_1_out));  // open: cin, cout
  Multiplexer #(.width(8)) multiplexer_1 (
    .in0(adder_1_out), .in1(Data_In), .out(multiplexer_1_out), .sel(Load));  // open: en
  or or_1 (or_1_out, Load, comparator_1_gt);
  Comparator #(.mode("unsigned")) comparator_1 (.a(Address), .b({8{1'b0}}), .gt(comparator_1_gt));  // open: eq, lt
  Multiplexer #(.width(8)) multiplexer_2 (
    .in0(multiplexer_1_out), .in1({8{1'b0}}), .out(multiplexer_2_out), .sel(Reset));  // open: en
  Register register_1 (.D(multiplexer_2_out), .en(or_1_out), .Q(Address), .clk(Clock));  // open: clr
endmodule

module Generate_Ready (
  input  [7:0] Address,
  output Ready
);

  Comparator comparator_1 (.a(Address), .b({8{1'b0}}), .eq(Ready));  // open: gt, lt
endmodule

module Operand_Select (
  input  [3:0] A_Operand,
  input  [3:0] B_Operand,
  input  [3:0] C_Operand,
  input  [1:0] Operand_Selector,
  output [3:0] Constant
);

  Multiplexer #(.select(2), .width(4)) multiplexer_1 (
    .in0(4'b0000), .in1(A_Operand), .in2(B_Operand), .in3(C_Operand), .out(Constant), .sel(Operand_Selector));  // open: en
endmodule

module Microprocessor (
  input  [15:0] Instruction,
  input  Start,
  input  [3:0] Data_In,
  input  Reset,
  input  Clock,
  output [3:0] Address_Out,
  output [3:0] Data_Out,
  output WriteEnable,
  output Ready,
  output CLK
);

  wire [2:0] datapath_1_pzn;
  wire [3:0] control_unit_1_constant;
  wire [15:0] control_unit_1_control_word;

  Control_Unit control_unit_1 (
    .Instruction(Instruction), .Start(Start), .Reset(Reset), .Clock(Clock),
    .Constant(control_unit_1_constant), .Control_Word(control_unit_1_control_word), .PZN(datapath_1_pzn),
    .Memory_Write(WriteEnable), .Ready(Ready));
  Datapath datapath_1 (
    .CLK(Clock), .ConstIN(control_unit_1_constant), .AddrOut(Address_Out), .DataOut(Data_Out),
    .PZN(datapath_1_pzn), .DataIN(Data_In), .Control_Word(control_unit_1_control_word));

  assign CLK = Clock;
endmodule

module MP_w__Ram (
  input  [15:0] Instruction,
  input  Start,
  input  Reset,
  output Ready
);

  wire Clock_out, microprocessor_1_clk, microprocessor_1_writeenable;
  wire [3:0] microprocessor_1_address_out, microprocessor_1_data_out, ram_1_data;

  Clock Clock (.out(Clock_out));
  Microprocessor microprocessor_1 (
    .Instruction(Instruction), .Start(Start), .Reset(Reset), .Clock(Clock_out),
    .Address_Out(microprocessor_1_address_out), .Data_Out(microprocessor_1_data_out),
    .WriteEnable(microprocessor_1_writeenable), .Ready(Ready), .CLK(microprocessor_1_clk),
    .Data_In(ram_1_data));
  RAM #(.addrWidth(4), .dataWidth(4), .bus("separate")) ram_1 (
    .addr(microprocessor_1_address_out), .din(microprocessor_1_data_out), .data(ram_1_data),
    .str(microprocessor_1_writeenable), .clk(microprocessor_1_clk));  // open: sel, ld, clr
endmodule
