// Logisim project Design 1.circ as structural Verilog: 1 circuit, main circuit main
module main (
  input  I7,
  input  I6,
  input  I5,
  input  I4,
  input  I3,
  input  I2,
  input  I1,
  input  I0,
  input  I15,
  input  I14,
  input  I13,
  input  I12,
  input  I11,
  input  I10,
  input  I9,
  input  I8,
  input  [3:0] A0_A1_B0_B1,
  input  I7_2,
  input  I6_2,
  input  I5_2,
  input  I4_2,
  input  I3_2,
  input  I2_2,
  input  I1_2,
  input  I0_2,
  input  I15_2,
  input  I14_2,
  input  I13_2,
  input  I12_2,
  input  I11_2,
  input  I10_2,
  input  I9_2,
  input  I8_2,
  output C1,
  output C0
);

  Multiplexer #(.select(4), .enable("false")) multiplexer_1 (
    .in0(I0), .in1(I1), .in2(I2), .in3(I3), .in4(I4), .in5(I5), .in6(I6), .in7(I7), .in8(I15), .in9(I14),
    .in10(I13), .in11(I12), .in12(I11), .in13(I10), .in14(I9), .in15(I8), .out(C1), .sel(A0_A1_B0_B1));
  Multiplexer #(.select(4), .enable("false")) multiplexer_2 (
    .in0(I0_2), .in1(I1_2), .in2(I2_2), .in3(I3_2), .in4(I4_2), .in5(I5_2), .in6(I6_2), .in7(I7_2),
    .in8(I15_2), .in9(I14_2), .in10(I13_2), .in11(I12_2), .in12(I11_2), .in13(I10_2), .in14(I9_2),
    .in15(I8_2), .out(C0), .sel(A0_A1_B0_B1));
endmodule
