// Logisim project Design 2.circ as structural Verilog: 1 circuit, main circuit main
module main (
  input  B0,
  input  B1,
  input  A0,
  input  A1,
  input  I0,
  input  I1,
  input  I2,
  input  I3,
  input  I4,
  input  I5,
  input  I6,
  input  I7,
  input  I8,
  input  I9,
  input  I10,
  input  I11,
  input  I12,
  input  I13,
  input  I14,
  input  I15,
  input  I0_2,
  input  I1_2,
  input  I2_2,
  input  I3_2,
  input  I4_2,
  input  I5_2,
  input  I6_2,
  input  I7_2,
  input  I8_2,
  input  I9_2,
  input  I10_2,
  input  I11_2,
  input  I12_2,
  input  I13_2,
  input  I14_2,
  input  I15_2,
  output C1,
  output C0
);

  wire multiplexer_1_out, multiplexer_2_out, multiplexer_3_out, multiplexer_4_out, multiplexer_5_out,
       multiplexer_6_out, multiplexer_7_out, multiplexer_8_out, multiplexer_9_out, multiplexer_10_out,
       multiplexer_11_out, multiplexer_12_out, multiplexer_13_out, multiplexer_14_out, multiplexer_15_out,
       multiplexer_16_out, multiplexer_17_out, multiplexer_18_out, multiplexer_19_out, multiplexer_20_out,
       multiplexer_21_out, multiplexer_22_out, multiplexer_23_out, multiplexer_24_out, multiplexer_25_out,
       multiplexer_26_out, multiplexer_27_out, multiplexer_28_out;

  Multiplexer #(.enable("false")) multiplexer_1 (.in0(I0), .in1(I1), .out(multiplexer_1_out), .sel(B0));
  Multiplexer #(.enable("false")) multiplexer_2 (.in0(I2), .in1(I3), .out(multiplexer_2_out), .sel(B0));
  Multiplexer #(.enable("false")) multiplexer_3 (.in0(I4), .in1(I5), .out(multiplexer_3_out), .sel(B0));
  Multiplexer #(.enable("false")) multiplexer_4 (.in0(I6), .in1(I7), .out(multiplexer_4_out), .sel(B0));
  Multiplexer #(.enable("false")) multiplexer_5 (.in0(I8), .in1(I9), .out(multiplexer_5_out), .sel(B0));
  Multiplexer #(.enable("false")) multiplexer_6 (.in0(I10), .in1(I11), .out(multiplexer_6_out), .sel(B0));
  Multiplexer #(.enable("false")) multiplexer_7 (.in0(I12), .in1(I13), .out(multiplexer_7_out), .sel(B0));
  Multiplexer #(.enable("false")) multiplexer_8 (.in0(I14), .in1(I15), .out(multiplexer_8_out), .sel(B0));
  Multiplexer #(.enable("false")) multiplexer_9 (.in0(I0_2), .in1(I1_2), .out(multiplexer_9_out), .sel(B0));
  Multiplexer #(.enable("false")) multiplexer_10 (.in0(I2_2), .in1(I3_2), .out(multiplexer_10_out), .sel(B0));
  Multiplexer #(.enable("false")) multiplexer_11 (.in0(I4_2), .in1(I5_2), .out(multiplexer_11_out), .sel(B0));
  Multiplexer #(.enable("false")) multiplexer_12 (.in0(I6_2), .in1(I7_2), .out(multiplexer_12_out), .sel(B0));
  Multiplexer #(.enable("false")) multiplexer_13 (.in0(I8_2), .in1(I9_2), .out(multiplexer_13_out), .sel(B0));
  Multiplexer #(.enable("false")) multiplexer_14 (.in0(I10_2), .in1(I11_2), .out(multiplexer_14_out), .sel(B0));
  Multiplexer #(.enable("false")) multiplexer_15 (.in0(I12_2), .in1(I13_2), .out(multiplexer_15_out), .sel(B0));
  Multiplexer #(.enable("false")) multiplexer_16 (.in0(I14_2), .in1(I15_2), .out(multiplexer_16_out), .sel(B0));
  Multiplexer #(.enable("false")) multiplexer_17 (
    .in0(multiplexer_1_out), .in1(multiplexer_2_out), .out(multiplexer_17_out), .sel(B1));
  Multiplexer #(.enable("false")) multiplexer_18 (
    .in0(multiplexer_3_out), .in1(multiplexer_4_out), .out(multiplexer_18_out), .sel(B1));
  Multiplexer #(.enable("false")) multiplexer_19 (
    .in0(multiplexer_5_out), .in1(multiplexer_6_out), .out(multiplexer_19_out), .sel(B1));
  Multiplexer #(.enable("false")) multiplexer_20 (
    .in0(multiplexer_7_out), .in1(multiplexer_8_out), .out(multiplexer_20_out), .sel(B1));
  Multiplexer #(.enable("false")) multiplexer_21 (
    .in0(multiplexer_9_out), .in1(multiplexer_10_out), .out(multiplexer_21_out), .sel(B1));
  Multiplexer #(.enable("false")) multiplexer_22 (
    .in0(multiplexer_11_out), .in1(multiplexer_12_out), .out(multiplexer_22_out), .sel(B1));
  Multiplexer #(.enable("false")) multiplexer_23 (
    .in0(multiplexer_13_out), .in1(multiplexer_14_out), .out(multiplexer_23_out), .sel(B1));
  Multiplexer #(.enable("false")) multiplexer_24 (
    .in0(multiplexer_15_out), .in1(multiplexer_16_out), .out(multiplexer_24_out), .sel(B1));
  Multiplexer #(.enable("false")) multiplexer_25 (
    .in0(multiplexer_17_out), .in1(multiplexer_18_out), .out(multiplexer_25_out), .sel(A0));
  Multiplexer #(.enable("false")) multiplexer_26 (
    .in0(multiplexer_19_out), .in1(multiplexer_20_out), .out(multiplexer_26_out), .sel(A0));
  Multiplexer #(.enable("false")) multiplexer_27 (
    .in0(multiplexer_21_out), .in1(multiplexer_22_out), .out(multiplexer_27_out), .sel(A0));
  Multiplexer #(.enable("false")) multiplexer_28 (
    .in0(multiplexer_23_out), .in1(multiplexer_24_out), .out(multiplexer_28_out), .sel(A0));
  Multiplexer #(.enable("false")) multiplexer_29 (
    .in0(multiplexer_25_out), .in1(multiplexer_26_out), .out(C1), .sel(A1));
  Multiplexer #(.enable("false")) multiplexer_30 (
    .in0(multiplexer_27_out), .in1(multiplexer_28_out), .out(C0), .sel(A1));

  // Notes on the sheet:
  //   C1
  //   C0
endmodule
