// Logisim project Design 3.circ as structural Verilog
module NAND (
  input  A1,
  input  A0,
  input  B1,
  input  B0,
  output C1,
  output C0
);

  wire nand_1_out, nand_2_out, nand_3_out, nand_4_out, nand_6_out, nand_7_out, nand_8_out, nand_9_out;

  nand nand_1 (nand_1_out, A1, A1);
  nand nand_2 (nand_2_out, B1, B1);
  nand nand_3 (nand_3_out, A1, A1);
  nand nand_4 (nand_4_out, B1, B1);
  nand nand_5 (C1, nand_3_out, nand_4_out);
  nand nand_6 (nand_6_out, nand_1_out, B0);
  nand nand_7 (nand_7_out, A1, A0);
  nand nand_8 (nand_8_out, nand_2_out, A0);
  nand nand_9 (nand_9_out, B1, B0);
  nand nand_10 (C0, nand_6_out, nand_7_out, nand_8_out, nand_9_out);
endmodule
