// Logisim project Design 4.circ as structural Verilog: 1 circuit, main circuit table
module \table  (
  input  Anow,
  input  Bnow,
  input  Abefore,
  input  Bbefore,
  output Coutput,
  output Acarry,
  output Bcarry
);

  wire and_1_out, and_2_out, and_3_out, and_4_out, and_5_out, and_6_out, and_7_out, and_8_out, and_9_out,
       and_10_out, not_1_out, not_2_out, not_3_out, not_4_out, not_5_out, not_6_out;

  and and_1 (and_1_out, Abefore, Anow);
  not not_1 (not_1_out, Abefore);
  and and_2 (and_2_out, not_1_out, Bnow);
  not not_2 (not_2_out, Bbefore);
  and and_3 (and_3_out, not_2_out, Anow);
  and and_4 (and_4_out, Bbefore, Bnow);
  and and_5 (and_5_out, Abefore, not_3_out);
  not not_3 (not_3_out, Bbefore);
  and and_6 (and_6_out, Anow, not_4_out);
  not not_4 (not_4_out, Bbefore);
  and and_7 (and_7_out, Anow, Abefore);
  not not_5 (not_5_out, Abefore);
  and and_8 (and_8_out, not_5_out, Bbefore);
  and and_9 (and_9_out, Bnow, not_6_out);
  not not_6 (not_6_out, Abefore);
  and and_10 (and_10_out, Bnow, Bbefore);
  or or_1 (Coutput, and_1_out, and_2_out, and_3_out, and_4_out);
  or or_2 (Acarry, and_5_out, and_6_out, and_7_out);
  or or_3 (Bcarry, and_8_out, and_9_out, and_10_out);
endmodule
