// Logisim project Design 5.circ as structural Verilog: 2 circuits, main circuit main
module main (
  input  A3,
  input  A2,
  input  A1,
  input  A0,
  input  B3,
  input  B2,
  input  B1,
  input  B0,
  output C3,
  output C2,
  output C1,
  output C0
);

  wire diagram_1_acarry, diagram_1_bcarry, diagram_2_acarry, diagram_2_bcarry, diagram_3_acarry,
       diagram_3_bcarry;

  diagram diagram_1 (
    .Anow(A3), .Bnow(B3), .Abefore(1'b0), .Bbefore(1'b0), .Coutput(C3), .Acarry(diagram_1_acarry),
    .Bcarry(diagram_1_bcarry));
  diagram diagram_2 (
    .Anow(A2), .Bnow(B2), .Abefore(diagram_1_acarry), .Bbefore(diagram_1_bcarry), .Coutput(C2),
    .Acarry(diagram_2_acarry), .Bcarry(diagram_2_bcarry));
  diagram diagram_3 (
    .Anow(A1), .Bnow(B1), .Abefore(diagram_2_acarry), .Bbefore(diagram_2_bcarry), .Coutput(C1),
    .Acarry(diagram_3_acarry), .Bcarry(diagram_3_bcarry));
  diagram diagram_4 (
    .Anow(A0), .Bnow(B0), .Abefore(diagram_3_acarry), .Bbefore(diagram_3_bcarry), .Coutput(C0));  // open: Acarry, Bcarry
endmodule

module diagram (
  input  Anow,
  input  Bnow,
  input  Abefore,
  input  Bbefore,
  output Coutput,
  output Acarry,
  output Bcarry
);

  wire and_1_out, and_2_out, and_3_out, and_4_out, and_5_out, and_6_out, and_7_out, and_8_out, and_9_out,
       and_10_out, not_1_out, not_2_out, not_3_out, not_4_out, not_5_out, not_6_out;

  and and_1 (and_1_out, Abefore, Anow);
  not not_1 (not_1_out, Abefore);
  and and_2 (and_2_out, not_1_out, Bnow);
  not not_2 (not_2_out, Bbefore);
  and and_3 (and_3_out, not_2_out, Anow);
  and and_4 (and_4_out, Bbefore, Bnow);
  and and_5 (and_5_out, Abefore, not_3_out);
  not not_3 (not_3_out, Bbefore);
  and and_6 (and_6_out, Anow, not_4_out);
  not not_4 (not_4_out, Bbefore);
  and and_7 (and_7_out, Anow, Abefore);
  not not_5 (not_5_out, Abefore);
  and and_8 (and_8_out, not_5_out, Bbefore);
  and and_9 (and_9_out, Bnow, not_6_out);
  not not_6 (not_6_out, Abefore);
  and and_10 (and_10_out, Bnow, Bbefore);
  or or_1 (Coutput, and_1_out, and_2_out, and_3_out, and_4_out);
  or or_2 (Acarry, and_5_out, and_6_out, and_7_out);
  or or_3 (Bcarry, and_8_out, and_9_out, and_10_out);
endmodule
