// Logisim project Design 1.circ as structural Verilog: 1 circuit, main circuit main
module main (
  input  IN,
  output SHOT
);

  wire clock_1_out, d_ff_1_q;

  Clock clock_1 (.out(clock_1_out));
  D_Flip_Flop d_ff_1 (.clk(clock_1_out), .D(SHOT), .Q(d_ff_1_q), .preset(1'b0), .reset(1'b0));  // open: Qn, en
  or or_1 (SHOT, IN, d_ff_1_q);
endmodule
