// Logisim project Design 2.circ as structural Verilog: 1 circuit, main circuit main
module main (
  input  E,
  output T
);

  wire and_1_out, and_2_out, clock_1_out, d_ff_1_qn, not_1_out, or_1_out;

  Clock clock_1 (.out(clock_1_out));
  D_Flip_Flop d_ff_1 (.clk(clock_1_out), .D(or_1_out), .Q(T), .Qn(d_ff_1_qn), .preset(1'b0), .reset(1'b0));  // open: en
  not not_1 (not_1_out, E);
  and and_1 (and_1_out, not_1_out, T);
  and and_2 (and_2_out, d_ff_1_qn, E);
  or or_1 (or_1_out, and_1_out, and_2_out);
endmodule
