// Logisim project Design 3.circ as structural Verilog: 1 circuit, main circuit main
module main (
  input  X,
  input  in_2,
  output UNLOCK
);

  wire and_1_out, and_2_out, and_3_out, and_5_out, CLOCK_out, not_1_out, or_1_out, or_2_out, Q0_q, Q0_qn,
       Q1_q, Q1_qn;

  Clock CLOCK (.out(CLOCK_out));
  not not_1 (not_1_out, X);
  D_Flip_Flop Q0 (.clk(CLOCK_out), .D(or_2_out), .Q(Q0_q), .Qn(Q0_qn), .preset(1'b0), .en(in_2), .reset(1'b0));
  D_Flip_Flop Q1 (.clk(CLOCK_out), .D(or_1_out), .Q(Q1_q), .Qn(Q1_qn), .preset(1'b0), .en(in_2), .reset(1'b0));
  and and_1 (and_1_out, X, Q0_qn);
  and and_2 (and_2_out, X, Q1_q);
  and and_3 (and_3_out, Q1_q, Q0_qn);
  and and_4 (UNLOCK, Q1_qn, Q0_q);
  and and_5 (and_5_out, Q1_q, not_1_out);
  or or_1 (or_1_out, and_1_out, and_2_out, and_3_out);
  or or_2 (or_2_out, UNLOCK, and_5_out);
endmodule
