// Logisim project Design 6.circ as structural Verilog: 1 circuit, main circuit main
module main (
  input  A,
  input  B,
  input  ENABLE,
  output DIRECTION,
  output VALID
);

  wire and_1_out, and_2_out, and_3_out, and_4_out, and_5_out, and_6_out, CLOCK_out, not_1_out, not_2_out,
       not_3_out, not_4_out, not_5_out, Q0_q, Q0_qn, Q1_q, Q1_qn;

  Clock CLOCK (.out(CLOCK_out));
  D_Flip_Flop Q1 (.clk(CLOCK_out), .D(A), .Q(Q1_q), .Qn(Q1_qn), .preset(1'b0), .en(ENABLE), .reset(1'b0));
  D_Flip_Flop Q0 (.clk(CLOCK_out), .D(B), .Q(Q0_q), .Qn(Q0_qn), .preset(1'b0), .en(ENABLE), .reset(1'b0));
  not not_1 (not_1_out, B);
  not not_2 (not_2_out, A);
  not not_3 (not_3_out, A);
  not not_4 (not_4_out, A);
  not not_5 (not_5_out, B);
  and and_1 (and_1_out, not_1_out, Q1_qn, ENABLE);
  and and_2 (and_2_out, Q1_q, B, ENABLE);
  and and_3 (and_3_out, not_2_out, not_3_out, Q0_q, ENABLE);
  and and_4 (and_4_out, not_4_out, B, Q0_q, ENABLE);
  and and_5 (and_5_out, A, A, Q0_qn, ENABLE);
  and and_6 (and_6_out, A, not_5_out, Q0_qn, ENABLE);
  or or_1 (DIRECTION, and_1_out, and_2_out);
  or or_2 (VALID, and_3_out, and_4_out, and_5_out, and_6_out);
endmodule
