// Logisim project Spinner.circ as structural Verilog: 1 circuit, main circuit main
module main (
  input  ENABLE,
  input  A0,
  input  B0,
  input  A1,
  input  B1,
  output out_6
);

  wire clock_1_out, d_ff_1_q, d_ff_2_q, d_ff_3_q, d_ff_4_q, d_ff_5_q, multiplexer_1_out, xnor_1_out,
       xor_1_out, xor_2_out, xor_3_out;

  Clock clock_1 (.out(clock_1_out));
  D_Flip_Flop d_ff_1 (.clk(clock_1_out), .D(A0), .Q(d_ff_1_q), .preset(1'b0), .en(ENABLE), .reset(1'b0));  // open: Qn
  D_Flip_Flop d_ff_2 (.clk(clock_1_out), .D(B0), .Q(d_ff_2_q), .preset(1'b0), .en(ENABLE), .reset(1'b0));  // open: Qn
  D_Flip_Flop d_ff_3 (.clk(clock_1_out), .D(A1), .Q(d_ff_3_q), .preset(1'b0), .en(ENABLE), .reset(1'b0));  // open: Qn
  D_Flip_Flop d_ff_4 (.clk(clock_1_out), .D(B1), .Q(d_ff_4_q), .preset(1'b0), .en(ENABLE), .reset(1'b0));  // open: Qn
  xor xor_1 (xor_1_out, d_ff_1_q, d_ff_3_q);
  xor xor_2 (xor_2_out, d_ff_2_q, d_ff_4_q);
  xnor xnor_1 (xnor_1_out, d_ff_1_q, d_ff_4_q);
  xor xor_3 (xor_3_out, xor_1_out, xor_2_out);
  Multiplexer #(.enable("false")) multiplexer_1 (
    .in1(xor_3_out), .out(multiplexer_1_out), .sel(xor_3_out));  // open: in0
  D_Flip_Flop d_ff_5 (
    .clk(clock_1_out), .D(xnor_1_out), .Q(d_ff_5_q), .preset(1'b0), .en(multiplexer_1_out), .reset(1'b0));  // open: Qn
  assign out_6 = multiplexer_1_out ? d_ff_5_q : 1'bz;  // Controlled_Buffer controlled_buffer_1
endmodule
