// Logisim project MEALY.circ as structural Verilog: 1 circuit, main circuit main
module main (
  input  IN,
  output UNLOCK
);

  wire and_1_out, and_2_out, and_3_out, and_4_out, and_5_out, and_6_out, and_7_out, and_8_out, clock_1_out,
       not_1_out, not_2_out, or_2_out, or_3_out, Q0_q, Q0_qn, Q1_q, Q1_qn, Q2_q, Q2_qn;

  Clock clock_1 (.out(clock_1_out));
  D_Flip_Flop Q2 (.clk(clock_1_out), .D(and_3_out), .Q(Q2_q), .Qn(Q2_qn), .preset(1'b0), .reset(1'b0));  // open: en
  D_Flip_Flop Q1 (.clk(clock_1_out), .D(or_2_out), .Q(Q1_q), .Qn(Q1_qn), .preset(1'b0), .reset(1'b0));  // open: en
  D_Flip_Flop Q0 (.clk(clock_1_out), .D(or_3_out), .Q(Q0_q), .Qn(Q0_qn), .preset(1'b0), .reset(1'b0));  // open: en
  not not_1 (not_1_out, IN);
  not not_2 (not_2_out, IN);
  and and_1 (and_1_out, IN, Q2_qn, Q1_q, Q0_q);
  and and_2 (and_2_out, not_1_out, Q2_qn, Q1_q, Q0_q);
  and and_3 (and_3_out, Q1_q, Q0_q, IN);
  and and_4 (and_4_out, Q2_q, Q0_q);
  and and_5 (and_5_out, Q1_qn, Q0_q, IN);
  and and_6 (and_6_out, Q1_q, Q1_qn);
  and and_7 (and_7_out, Q1_q, Q0_qn, not_2_out);
  and and_8 (and_8_out, Q2_qn, Q1_qn, Q0_qn, IN);
  or or_1 (UNLOCK, and_1_out, and_2_out);
  or or_2 (or_2_out, and_4_out, and_5_out, and_6_out);
  or or_3 (or_3_out, and_7_out, and_8_out);
endmodule
