// Logisim project MEALY2.circ as structural Verilog: 1 circuit, main circuit main
module main (
  input  IN,
  output UNLOCK
);

  wire clock_1_out, Q0_q, Q0_qn, Q1_q, Q2_q;

  Clock clock_1 (.out(clock_1_out));
  D_Flip_Flop Q2 (.clk(clock_1_out), .D(Q1_q), .Q(Q2_q), .preset(1'b0), .reset(1'b0));  // open: Qn, en
  D_Flip_Flop Q1 (.clk(clock_1_out), .D(Q0_q), .Q(Q1_q), .preset(1'b0), .reset(1'b0));  // open: Qn, en
  D_Flip_Flop Q0 (.clk(clock_1_out), .D(IN), .Q(Q0_q), .Qn(Q0_qn), .preset(1'b0), .reset(1'b0));  // open: en
  and and_1 (UNLOCK, IN, Q2_q, Q1_q, Q0_qn);
endmodule
