// Logisim project LAB 8.circ as structural Verilog: 2 circuits, main circuit main
module main (
  input  GO,
  input  [3:0] IN,
  input  [1:0] F,
  output [3:0] OUT
);

  wire and_1_out, clock_1_out, d_ff_1_qn;
  wire [3:0] adder_1_out, multiplexer_1_out, multiplier_1_out, subtractor_1_out;

  Clock clock_1 (.out(clock_1_out));
  and and_1 (and_1_out, GO, d_ff_1_qn);
  D_Flip_Flop d_ff_1 (.clk(clock_1_out), .D(GO), .Qn(d_ff_1_qn));  // open: Q, preset, en, reset
  Adder #(.width(4)) adder_1 (.a(OUT), .b(IN), .out(adder_1_out));  // open: cin, cout
  Subtractor #(.width(4)) subtractor_1 (.a(OUT), .b(IN), .out(subtractor_1_out));  // open: bin, bout
  Multiplier #(.width(4)) multiplier_1 (.a(OUT), .b(IN), .out(multiplier_1_out));  // open: cin, cout
  Multiplexer #(.select(2), .width(4)) multiplexer_1 (
    .in0(IN), .in1(adder_1_out), .in2(subtractor_1_out), .in3(multiplier_1_out), .out(multiplexer_1_out),
    .sel(F));  // open: en
  Register #(.width(4)) register_1 (.D(multiplexer_1_out), .en(and_1_out), .Q(OUT), .clk(clock_1_out));  // open: clr
endmodule

module OVERALL (
  input  GO,
  input  [3:0] IN,
  input  [1:0] F,
  output [3:0] OUT
);

  main main_1 (.GO(GO), .IN(IN), .F(F), .OUT(OUT));
endmodule
