// Logisim project LAB 9 V2.circ as structural Verilog: 1 circuit, main circuit main
module main (
  input  C,
  input  RESET,
  input  in_3
);

  wire and_1_out, clock_1_out, comparator_1_eq, not_1_out, or_1_out;
  wire [2:0] register_1_q, register_2_q;
  wire [5:0] counter_1_q, multiplexer_1_out, rom_1_data;

  Clock clock_1 (.out(clock_1_out));
  not not_1 (not_1_out, C);
  and and_1 (and_1_out, comparator_1_eq, not_1_out);
  or or_1 (or_1_out, and_1_out, RESET);
  Counter #(.width(6), .max('h27)) counter_1 (
    .load(or_1_out), .D(6'b001111), .Q(counter_1_q), .clk(clock_1_out));  // open: count, carry, clr
  Comparator #(.width(6)) comparator_1 (.a(6'b001111), .b(counter_1_q), .eq(comparator_1_eq));  // open: gt, lt
  Multiplexer #(.width(6)) multiplexer_1 (
    .in0(counter_1_q), .in1(6'b010011), .out(multiplexer_1_out), .sel(RESET));  // open: en
  ROM #(.addrWidth(6), .dataWidth(6)) rom_1 (.addr(multiplexer_1_out), .data(rom_1_data));  // open: sel
  Register #(.width(3)) register_1 (.D(rom_1_data[2:0]), .en(in_3), .Q(register_1_q), .clk(clock_1_out));  // open: clr
  Register #(.width(3)) register_2 (.D(rom_1_data[5:3]), .en(in_3), .Q(register_2_q), .clk(clock_1_out));  // open: clr
  LED HLR (.in(register_1_q[0]));
  LED HLY (.in(register_1_q[1]));
  LED HLG (.in(register_1_q[2]));
  LED FLR (.in(register_2_q[0]));
  LED FLY (.in(register_2_q[1]));
  LED FLG (.in(register_2_q[2]));

  // Notes on the sheet:
  //   contents of rom_1 (hex, n*v repeats v):
  //   16*c a a a 9 16*21 11 11 11 9
endmodule
