// Logisim project LAB 9.circ as structural Verilog: 1 circuit, main circuit main
module main (
  input  C,
  input  RESET,
  input  in_3
);

  wire and_1_out, and_2_out, and_3_out, and_4_out, and_5_out, and_6_out, clock_1_out, comparator_1_eq,
       counter_1_carry, counter_2_carry, counter_3_carry, counter_4_carry, counter_5_carry, not_1_out,
       or_1_out, or_2_out, or_3_out, or_4_out;
  wire [2:0] counter_6_q, multiplexer_1_out, register_1_q, register_2_q;
  wire [5:0] rom_1_data;

  Counter #(.width(1), .max('h1)) counter_1 (
    .count(and_3_out), .carry(counter_1_carry), .clk(clock_1_out), .clr(or_1_out));  // open: load, D, Q
  Clock clock_1 (.out(clock_1_out));
  or or_1 (or_1_out, and_6_out, and_4_out);
  not not_1 (not_1_out, C);
  Counter #(.width(2), .max('h3)) counter_2 (
    .count(and_2_out), .carry(counter_2_carry), .clk(clock_1_out), .clr(and_3_out));  // open: load, D, Q
  Counter #(.width(2), .max('h3)) counter_3 (
    .count(and_5_out), .carry(counter_3_carry), .clk(clock_1_out), .clr(and_3_out));  // open: load, D, Q
  and and_1 (and_1_out, comparator_1_eq, not_1_out);
  or or_2 (or_2_out, and_1_out, RESET);
  Counter #(.width(3), .max('h7)) counter_4 (
    .count(and_4_out), .carry(counter_4_carry), .clk(clock_1_out), .clr(or_3_out));  // open: load, D, Q
  or or_3 (or_3_out, and_2_out, and_5_out);
  or or_4 (or_4_out, counter_1_carry, counter_2_carry, counter_3_carry, counter_4_carry, counter_5_carry);
  Counter #(.width(4), .max('hf)) counter_5 (
    .count(and_6_out), .carry(counter_5_carry), .clk(clock_1_out), .clr(or_3_out));  // open: load, D, Q
  Counter #(.width(3), .max('h7)) counter_6 (
    .load(or_2_out), .D(3'b000), .count(or_4_out), .Q(counter_6_q), .clk(clock_1_out));  // open: carry, clr
  Comparator #(.width(3)) comparator_1 (.a(3'b000), .b(counter_6_q), .eq(comparator_1_eq));  // open: gt, lt
  Multiplexer #(.width(3)) multiplexer_1 (
    .in0(counter_6_q), .in1(3'b011), .out(multiplexer_1_out), .sel(RESET));  // open: en
  ROM #(.addrWidth(3), .dataWidth(6)) rom_1 (.addr(multiplexer_1_out), .data(rom_1_data));  // open: sel
  Register #(.width(3)) register_1 (.D(rom_1_data[2:0]), .en(in_3), .Q(register_1_q), .clk(clock_1_out));  // open: clr
  Register #(.width(3)) register_2 (.D(rom_1_data[5:3]), .en(in_3), .Q(register_2_q), .clk(clock_1_out));  // open: clr
  and and_2 (and_2_out, register_2_q[0], register_1_q[1]);
  and and_3 (and_3_out, register_2_q[0], register_1_q[0]);
  and and_4 (and_4_out, register_2_q[0], register_1_q[2]);
  and and_5 (and_5_out, register_2_q[1], register_1_q[0]);
  LED HLR (.in(register_1_q[0]));
  LED HLY (.in(register_1_q[1]));
  LED HLG (.in(register_1_q[2]));
  LED FLR (.in(register_2_q[0]));
  LED FLY (.in(register_2_q[1]));
  LED FLG (.in(register_2_q[2]));
  and and_6 (and_6_out, register_2_q[2], register_1_q[0]);

  // Notes on the sheet:
  //   contents of rom_1 (hex, n*v repeats v):
  //   c a 9 9 21 11 9 c
endmodule
